# Fritzing sketch clock (saved by Fritzing 1.0.5)
breadboards: 3

parts:
  NEOPIXEL1 = Neopixel Strip -- White (30/m) [part_number=1376]
  Pico_H1 = Raspberry Pi Pico H
  Q1 = LTR-301 [package=ltr-301]
  R1 = Resistor [tolerance=±5% resistance=10k power=0.25W package=THT]
  DS1 = DS18B20 1-Wire Temperature Sensor [part_number=DS18B20]
  R2 = Resistor [tolerance=±5% resistance=4.7k power=0.25W package=THT]
  U1 = POT [knob_status=50% power=0.5W package=alps_pot]
  LCD1 = LCD screen
  IC1 = DIP - 22 pins [chip_label="i2c backpack" package="DIP (Dual Inline) [THT]"]
  PCB2 = RTC_DS1302_module
  DHT1 = DHT11 Humitidy and Temperature Sensor
  R3 = Resistor [tolerance=±5% power=0.25W resistance=10k package=THT]
  R4 = Resistor [tolerance=±5% power=0.25W resistance=10k package=THT]
  S1 = Pushbutton [package="[THT]"]
  S2 = Pushbutton [package="[THT]"]

nets:
  N1: NEOPIXEL1.+5V, Pico_H1.VBUS, IC1.VCC#1
  N2: NEOPIXEL1.Dout, Pico_H1.GP28_A2
  GND: NEOPIXEL1.GND, Pico_H1.GND, IC1.GND, PCB2.GND, S1.Pin_1, S1.Pin_2, S2.Pin_1, S2.Pin_2
  VDD: Pico_H1.3V3, Q1.C, DS1.VDD, R2.Pin_0, U1.E, PCB2.VCC, DHT1.VDD, R3.Pin_0, R4.Pin_0
  N3: Pico_H1.GP27_A1, Q1.E, R1.Pin_0
  N4: Pico_H1.GP26_A0, U1.S
  N5: Pico_H1.GP22, DHT1.DATA, R3.Pin_1, R4.Pin_1
  N6: Pico_H1.GP20, DS1.DQ, R2.Pin_1
  N7: Pico_H1.GP19, PCB2.CLK
  N8: Pico_H1.GP18, PCB2.DAT
  N9: Pico_H1.GP17, PCB2.RST
  N10: Pico_H1.GP15, IC1.SCL
  N11: Pico_H1.GP14, IC1.SDA
  N12: Pico_H1.GP1, S2.Pin_3, S2.Pin_4
  N13: Pico_H1.GP0, S1.Pin_3, S1.Pin_4
  GND_2: R1.Pin_1, DS1.GND, U1.A, DHT1.GND
  VSS: LCD1.VSS, IC1.VSS
  N14: LCD1.VDD, IC1.VCC#7
  N15: LCD1.V0, IC1.V0
  N16: LCD1.RS, IC1.RS
  N17: LCD1.R/W, IC1.RW

custom parts:
  Neopixel Strip -- White (30/m): These NeoPixel strips have 30 digitally-addressable pixel LEDs per meter and are very affordable and are only 12.5 mm wide, 10 mm if you remove the strip from the casing.
  Raspberry Pi Pico H: Raspberry Pi Pico H. Based around the RP2040 microcontroller the Pico H is a low cost microcontroller device bringing Raspberry Pi quality, cost, and easy of use to the microcontroller space.
  DIP - 22 pins: A DIP stand-in part for whatever IC you want. With 22 pins on a 300mil dual inline package (DIP) footprint.
  RTC_DS1302_module: Arduino module DS1302 SPI Real Time Clock
  DHT11 Humitidy and Temperature Sensor: DHT11 Humidity and Temperature Sensor
